# Fritzing sketch Circuito (saved by Fritzing 0.9.3b)
circuit board: 8.46667cm x 5.64444cm
breadboards: 1

parts:
  S1 = Pushbutton [package="[THT]"]
  R1 = Resistor [tolerance=±5% resistance=220 package=THT]
  LED1 = LED - 5mm [color="Red (633nm)" package="5 mm [THT]"]
  R2 = Resistor [tolerance=±5% resistance=220 package=THT]
  S2 = Pushbutton [package="[THT]"]
  R3 = Resistor [tolerance=±5% resistance=220 package=THT]
  U1 = ESP8266 NodeMCU LoLin base

nets:
  N1: S1.Pin_1, S1.Pin_2, R1.Pin_0, U1.D3-2, U1.D3-3
  N2: S1.Pin_3, S1.Pin_4, LED1.cathode, S2.Pin_3, S2.Pin_4, U1.5V-0, U1.5V-2
  N3: R1.Pin_1, R2.Pin_1, R3.Pin_1, U1.GND2-0, U1.GND8-4, U1.GND8-5, U1.GND8-8, U1.GND8-9, U1.GND8-10, U1.GND8-11
  N4: LED1.anode, R2.Pin_0, U1.D1-0, U1.D1-1
  N5: S2.Pin_1, S2.Pin_2, R3.Pin_0, U1.D2-0, U1.D2-3

custom parts:
  ESP8266 NodeMCU LoLin base: ESP8266 based NodeMCU Base
